# Fritzing sketch 01_dual_color_led (saved by Fritzing 0.9.2b)
breadboards: 1

parts:
  T-Cobbler1 = T-Cobbler
  module1 = Dule-Color LED

nets:
  N1: T-Cobbler1.GPIO17, module1.R
  N2: T-Cobbler1.GND#22, module1.GND
  N3: T-Cobbler1.GPIO18, module1.G

notes:
  Dual-Color LED

custom parts:
  T-Cobbler: T-Cobbler for RPi B+ and Rpi2 from SunFounder
  Dule-Color LED: DuleColor LED module of SunFounder Sensor Kit
