# Fritzing sketch 08_Vibration Switch (saved by Fritzing 0.8.7b)
breadboards: 1

parts:
  T-Cobbler1 = T-Cobbler
  module5 = Dule-Color LED
  module8 = Vibration Switch

nets:
  N1: T-Cobbler1.GPIO17, module8.SIG
  N2: T-Cobbler1.GPIO27, module5.G
  N3: T-Cobbler1.5V0#20, module8.VCC
  GND: T-Cobbler1.GND#22, module5.GND, module8.GND
  N4: T-Cobbler1.GPIO18, module5.R

notes:
  Vibration Switch
  Dual-color LED

custom parts:
  T-Cobbler: T-Cobbler for RPi B+ and Rpi2 from SunFounder
  Dule-Color LED: DuleColor LED module of SunFounder Sensor Kit
