# Fritzing sketch 25_Ultrasonic_Ranging (saved by Fritzing 0.9.2b)
breadboards: 1

parts:
  T-Cobbler1 = T-Cobbler
  元件1 = SRF05 Ultrasonic Rangefinder

nets:
  N1: T-Cobbler1.GPIO17, 元件1.Trig
  N2: T-Cobbler1.5V0#20, 元件1.VCC
  N3: T-Cobbler1.GND#22, 元件1.GND
  N4: T-Cobbler1.GPIO18, 元件1.Echo

notes:
  Ultrasonic Ranging

custom parts:
  T-Cobbler: T-Cobbler for RPi B+ and Rpi2 from SunFounder
